// Logisim project 32bitAdder.circ as structural Verilog: 4 circuits, main circuit CLA4电路
// CLA4
module \CLA4电路  (
  input  G4,
  input  P4,
  input  G3,
  input  P3,
  input  G2,
  input  P2,
  input  G1,
  input  P1,
  input  Cin,
  output C4,
  output C3,
  output C2,
  output C1,
  output G_star,
  output P_star
);

  wire and_1_out, and_2_out, and_4_out, and_5_out, and_6_out, and_7_out, and_8_out, and_9_out, and_10_out,
       and_11_out, and_12_out, and_13_out, and_14_out;

  and and_1 (and_1_out, P4, G3);
  or or_1 (G_star, and_1_out, and_2_out, and_4_out, G4);
  and and_2 (and_2_out, P4, P3, G2);
  and and_3 (P_star, P4, P3, P2, P1);
  and and_4 (and_4_out, P4, P3, P2, G1);
  and and_5 (and_5_out, P4, G3);
  or or_2 (C4, G4, and_5_out, and_6_out, and_8_out, and_7_out);
  and and_6 (and_6_out, P4, P3, G2);
  and and_7 (and_7_out, P4, P3, P2, P1, Cin);
  and and_8 (and_8_out, P4, P3, P2, G1);
  and and_9 (and_9_out, P3, G2);
  or or_3 (C3, G3, and_9_out, and_10_out, and_11_out);
  and and_10 (and_10_out, P3, P2, G1);
  and and_11 (and_11_out, P3, P2, P1, Cin);
  and and_12 (and_12_out, G1, P2);
  or or_4 (C2, G2, and_12_out, and_13_out);
  and and_13 (and_13_out, P2, P1, Cin);
  or or_5 (C1, G1, and_14_out);
  and and_14 (and_14_out, P1, Cin);

  // Notes on the sheet:
  //   输入引脚区
  //   请根据以上引脚以及隧道信号设计完成4位先行进位电路CLA4
  //   请在上述框图中完成CLA4的电路设计，该电路将作为4位先行进位加法器的子电路使用
  //   输出引脚区
  //   请勿增改引脚定义
endmodule

module \_4位快速加法器  (
  input  [3:0] X,
  input  [3:0] Y,
  input  Cin,
  output [3:0] S,
  output Cout,
  output Cn_1,
  output G_star,
  output P_star
);

  wire and_1_out, and_2_out, and_3_out, and_4_out, \cla4电路_1_c1 , \cla4电路_1_c2 , xor_2_out, xor_3_out,
       xor_5_out, xor_8_out;

  \CLA4电路  \cla4电路_1  (
    .G4(and_1_out), .P4(xor_2_out), .G3(and_2_out), .P3(xor_3_out), .G2(and_3_out), .P2(xor_5_out),
    .G1(and_4_out), .P1(xor_8_out), .Cin(Cin), .C4(Cout), .C3(Cn_1), .C2(\cla4电路_1_c2 ), .C1(\cla4电路_1_c1 ),
    .G_star(G_star), .P_star(P_star));
  and and_1 (and_1_out, X[3], Y[3]);
  xor xor_1 (S[3], Cn_1, xor_2_out);
  xor xor_2 (xor_2_out, X[3], Y[3]);
  and and_2 (and_2_out, X[2], Y[2]);
  xor xor_3 (xor_3_out, X[2], Y[2]);
  xor xor_4 (S[2], \cla4电路_1_c2 , xor_3_out);
  and and_3 (and_3_out, X[1], Y[1]);
  xor xor_5 (xor_5_out, X[1], Y[1]);
  xor xor_6 (S[1], \cla4电路_1_c1 , xor_5_out);
  and and_4 (and_4_out, X[0], Y[0]);
  // Probe on X
  // Probe on Y
  // Probe on S
  xor xor_7 (S[0], xor_8_out, Cin);
  xor xor_8 (xor_8_out, X[0], Y[0]);
  // Probe on X
  // Probe on Y
  // Probe on S

  // Notes on the sheet:
  //   输入引脚区
  //   输出引脚区
  //   注意：Cn-1的引出，是为了与Cout一起进行溢出Overflow判断的。但只有在完整的32位加法器中才需做溢出判断
  //   可自行查阅有关资料，了解有符号数的溢出判断机制。根据TinyMIPS，本实验将32位数加减法作为有符号数对待
  //   +
  //   =
  //   有符号加法
  //   +
  //   =
  //   无符号加法
endmodule

module \_16位快速加法器  (
  input  [15:0] X,
  input  [15:0] Y,
  input  Cin,
  output Cout,
  output Cn_1,
  output G_star,
  output P_star,
  output [15:0] S
);

  wire \cla4电路_1_c1 , \cla4电路_1_c2 , \cla4电路_1_c3 , \n4位快速加法器_1_g_star , \n4位快速加法器_1_p_star ,
       \n4位快速加法器_2_g_star , \n4位快速加法器_2_p_star , \n4位快速加法器_3_g_star , \n4位快速加法器_3_p_star ,
       \n4位快速加法器_4_g_star , \n4位快速加法器_4_p_star ;

  \CLA4电路  \cla4电路_1  (
    .G4(\n4位快速加法器_1_g_star ), .P4(\n4位快速加法器_1_p_star ), .G3(\n4位快速加法器_2_g_star ), .P3(\n4位快速加法器_2_p_star ),
    .G2(\n4位快速加法器_3_g_star ), .P2(\n4位快速加法器_3_p_star ), .G1(\n4位快速加法器_4_g_star ), .P1(\n4位快速加法器_4_p_star ),
    .Cin(Cin), .C4(Cout), .C3(\cla4电路_1_c3 ), .C2(\cla4电路_1_c2 ), .C1(\cla4电路_1_c1 ), .G_star(G_star),
    .P_star(P_star));
  \_4位快速加法器  \u_4位快速加法器_1  (
    .X(X[15:12]), .Y(Y[15:12]), .Cin(\cla4电路_1_c3 ), .S(S[15:12]), .G_star(\n4位快速加法器_1_g_star ),
    .P_star(\n4位快速加法器_1_p_star ), .Cn_1(Cn_1));  // open: Cout
  \_4位快速加法器  \u_4位快速加法器_2  (
    .X(X[11:8]), .Y(Y[11:8]), .Cin(\cla4电路_1_c2 ), .S(S[11:8]), .G_star(\n4位快速加法器_2_g_star ),
    .P_star(\n4位快速加法器_2_p_star ));  // open: Cout, Cn_1
  \_4位快速加法器  \u_4位快速加法器_3  (
    .X(X[7:4]), .Y(Y[7:4]), .Cin(\cla4电路_1_c1 ), .S(S[7:4]), .G_star(\n4位快速加法器_3_g_star ),
    .P_star(\n4位快速加法器_3_p_star ));  // open: Cout, Cn_1
  // Probe on X
  // Probe on Y
  // Probe on S
  // Probe on X
  // Probe on Y
  // Probe on S
  \_4位快速加法器  \u_4位快速加法器_4  (
    .X(X[3:0]), .Y(Y[3:0]), .Cin(Cin), .S(S[3:0]), .G_star(\n4位快速加法器_4_g_star ), .P_star(\n4位快速加法器_4_p_star ));  // open: Cout, Cn_1

  // Other names for the same wires on the sheet: S0[3:0] = S[3:0]; S1[3:0] = S[7:4]; S2[3:0] = S[11:8];
  //   S3[3:0] = S[15:12]; X0[3:0] = X[3:0]; X1[3:0] = X[7:4]; X2[3:0] = X[11:8]; X3[3:0] = X[15:12]; Y0[3:0] = Y[3:0];
  //   Y1[3:0] = Y[7:4]; Y2[3:0] = Y[11:8]; Y3[3:0] = Y[15:12]

  // Notes on the sheet:
  //   输入引脚区
  //   注意：要求该16为加法器也是先行进位的
  //   输出引脚区
  //   请在上述框图中完成16位快速加法器的电路设计，该电路将作为4位先行进位加法器的实现（使用4位加法器和CLA4作为子电路）
  //   +
  //   =
  //   有符号加法
  //   +
  //   =
  //   无符号加法
endmodule

module \_32位加法器  (
  input  Cin,
  input  Overflow,
  input  [31:0] in_3,
  input  [31:0] in_4,
  output [31:0] out_5
);

  wire \n16位快速加法器_1_cn_1 , \n16位快速加法器_1_cout , \n16位快速加法器_2_cout ;

  xor xor_1 (Overflow, \n16位快速加法器_1_cout , \n16位快速加法器_1_cn_1 );
  \_16位快速加法器  \u_16位快速加法器_1  (
    .X(in_3[31:16]), .Y(in_4[31:16]), .Cin(\n16位快速加法器_2_cout ), .S(out_5[31:16]), .Cout(\n16位快速加法器_1_cout ),
    .Cn_1(\n16位快速加法器_1_cn_1 ));  // open: G_star, P_star
  // Probe on in_3
  // Probe on in_4
  // Probe on out_5
  // Probe on in_3
  // Probe on in_4
  // Probe on out_5
  \_16位快速加法器  \u_16位快速加法器_2  (
    .X(in_3[15:0]), .Y(in_4[15:0]), .Cin(Cin), .S(out_5[15:0]), .Cout(\n16位快速加法器_2_cout ));  // open: Cn_1, G_star, P_star

  // Other names for the same wires on the sheet: OF = Overflow; S[31:0] = out_5; S0[15:0] = out_5[15:0];
  //   S1[15:0] = out_5[31:16]; X[31:0] = in_3; X0[15:0] = in_3[15:0]; X1[15:0] = in_3[31:16]; Y[31:0] = in_4;
  //   Y0[15:0] = in_4[15:0]; Y1[15:0] = in_4[31:16]

  // Notes on the sheet:
  //   X
  //   输入引脚区
  //   Y
  //   S
  //   该32位加法器用16位快速加法器作为子电路实现，不需要采用先行进位
  //   请参照前面子电路，先画出输入引脚区和输出引脚区，再画电路实现和加法器外观
  //   输出引脚区
  //   +
  //   =
  //   有符号加法
  //   +
  //   =
  //   无符号加法
endmodule
