// Logisim project MIPS-single-cycle-cpu.circ as structural Verilog: 5 circuits, main circuit ◇单周期MIPS(硬布线)
module \单周期MIPS_硬布线  (
);

  wire ALUSrc, Branch, CLK, Flag1, Jump, maincontrol_1_out_2, MemRead, MemToReg, MemWrite, mips_ram_1_p4,
       not_1_out, RegWrite, RST, Zero, \程序开关_out ;
  wire [1:0] ALUop;
  wire [2:0] ALUcontrol;
  wire [4:0] multiplexer_4_out;
  wire [15:0] \总周期数 , \无条件分支指令数 , \有条件分支成功跳转 ;
  wire [31:0] adder_1_out, adder_2_out, bit_extender_1_out, Ins, mips_alu_1_result, mips_regifile_1_r1,
       mips_regifile_1_r2, multiplexer_1_out, multiplexer_2_out, multiplexer_3_out, multiplexer_5_out,
       multiplexer_6_out, PC_q, shifter_1_out, shifter_3_out, shirftRes2, SyscallOut;

  Button \u_总复位  (.out(RST));
  Clock clock_1 (.out(CLK));
  Button \u_程序开关  (.out(\程序开关_out ));
  Register #(.width(32)) PC (.D(multiplexer_1_out), .Q(PC_q), .clk(CLK), .clr(RST));  // open: en
  Multiplexer #(.width(32)) multiplexer_1 (
    .in0(multiplexer_3_out), .in1(32'h2ffc), .out(multiplexer_1_out), .sel(\程序开关_out ));  // open: en
  Shifter #(.width(32), .shift("lr")) shifter_1 (.in(PC_q), .\dist (5'b00010), .out(shifter_1_out));
  Hex_Digit_Display hex_digit_display_1 (.value(SyscallOut[27:24]));  // open: dp
  Hex_Digit_Display hex_digit_display_2 (.value(SyscallOut[31:28]));  // open: dp
  Adder #(.width(32)) adder_1 (.a(32'h4), .b(PC_q), .out(adder_1_out), .cin(1'b0));  // open: cout
  Hex_Digit_Display hex_digit_display_3 (.value(SyscallOut[23:20]));  // open: dp
  Hex_Digit_Display hex_digit_display_4 (.value(SyscallOut[19:16]));  // open: dp
  Hex_Digit_Display hex_digit_display_5 (.value(SyscallOut[15:12]));  // open: dp
  Hex_Digit_Display hex_digit_display_6 (.value(SyscallOut[11:8]));  // open: dp
  Adder #(.width(32)) adder_2 (.a(adder_1_out), .b(shirftRes2), .out(adder_2_out), .cin(1'b0));  // open: cout
  ROM #(.addrWidth(24), .dataWidth(32)) rom_1 (.addr(shifter_1_out[23:0]), .data(Ins));  // open: sel
  Hex_Digit_Display hex_digit_display_7 (.value(SyscallOut[3:0]));  // open: dp
  Hex_Digit_Display hex_digit_display_8 (.value(SyscallOut[7:4]));  // open: dp
  Multiplexer #(.width(32)) multiplexer_2 (
    .in0(adder_1_out), .in1(adder_2_out), .out(multiplexer_2_out), .sel(Flag1));  // open: en
  Multiplexer #(.width(32)) multiplexer_3 (
    .in0(multiplexer_2_out), .in1({Ins[31:28], Ins[25:0], 2'b00}), .out(multiplexer_3_out), .sel(Jump));  // open: en
  Multiplexer #(.width(5)) multiplexer_4 (
    .in0(Ins[20:16]), .in1(Ins[15:11]), .out(multiplexer_4_out), .sel(maincontrol_1_out_2));  // open: en
  MainControl maincontrol_1 (
    .in_1(Ins[31:26]), .out_2(maincontrol_1_out_2), .out_3(ALUSrc), .out_4(MemToReg), .out_5(RegWrite),
    .out_6(MemRead), .out_7(MemWrite), .out_8(Branch), .out_9(ALUop), .PcSrc(Jump));
  not not_1 (not_1_out, CLK);
  assign bit_extender_1_out = {{16{Ins[15]}}, Ins[15:0]};  // Bit_Extender bit_extender_1
  // Probe on \总周期数 
  // Probe on \无条件分支指令数 
  // Probe on \有条件分支成功跳转 
  MIPS_Regifile mips_regifile_1 (
    .Din(multiplexer_6_out), .Clk(not_1_out), .R1(mips_regifile_1_r1), .R2(mips_regifile_1_r2),
    .WE(RegWrite), .W_num(multiplexer_4_out), .R1_num(Ins[25:21]), .R2_num(Ins[20:16]));
  Multiplexer #(.width(32)) multiplexer_5 (
    .in0(mips_regifile_1_r2), .in1(bit_extender_1_out), .out(multiplexer_5_out), .sel(ALUSrc));  // open: en
  Shifter #(.width(32)) shifter_2 (.in(bit_extender_1_out), .\dist (5'b00010), .out(shirftRes2));
  ALUcontrol alucontrol_1 (.Funct(Ins[5:0]), .ALUop(ALUop), .ALUControl(ALUcontrol));
  MIPS_ALU mips_alu_1 (
    .X(mips_regifile_1_r1), .Y(multiplexer_5_out), .AluOP(ALUcontrol), .Equal(Zero),
    .Result(mips_alu_1_result));  // open: Result_2
  Shifter #(.width(32), .shift("lr")) shifter_3 (.in(mips_alu_1_result), .\dist (5'b00010), .out(shifter_3_out));
  Counter #(.width(16), .max('hffff)) counter_1 (
    .D({16{1'b0}}), .count(1'b1), .Q(\总周期数 ), .clk(CLK), .clr(RST));  // open: load, carry
  and and_1 (Flag1, Branch, Zero);
  // MIPS_RAM mips_ram_1: pin names not known; wires that end beside it: shifter_3_out[23:0], mips_regifile_1_r2, MemWrite, mips_ram_1_p4, MemRead, RST, SyscallOut
  not not_2 (mips_ram_1_p4, CLK);
  Multiplexer #(.width(32)) multiplexer_6 (
    .in0(mips_alu_1_result), .in1(SyscallOut), .out(multiplexer_6_out), .sel(MemToReg));  // open: en

  // Notes on the sheet:
  //   指令存储器（ROM）
  //   CTRL+K  Command+K触发时钟连续仿真，程序运行结束后可停机，查看数据存储器中80单元的排序情况是有符号降序
  //   contents of rom_1 (hex, n*v repeats v):
  //   3072*0 8c080030 8c09002c 8c180028 308c022 2008024 208824 1310000d 3107822 2088020 2208824 11f1fffb
  //   2209020 8e4a0000 2288820 8e2b0000 14b602a 112cfff9 ae4b0000 ae2a0000 8000c0a
  //   数码管输出
  //   ALUcontrol
  //   地址右移
  //   外部存储器（RAM）
endmodule

module MIPS_Regifile (
  input  [31:0] Din,
  input  Clk,
  input  WE,
  input  [4:0] R1_num,
  input  [4:0] W_num,
  input  [4:0] R2_num,
  output [31:0] R1,
  output [31:0] R2
);

  // RegisterFile registerfile_1: pin names not known; wires that end beside it: Din, Clk, WE, W_num, R1_num, R2_num, R1, R2
endmodule

// ALU
module MIPS_ALU (
  input  [31:0] X,
  input  [31:0] Y,
  input  [2:0] AluOP,
  output Equal,
  output [31:0] Result,
  output [31:0] Result_2
);

  wire comparator_1_lt;
  wire [31:0] adder_1_out, and_1_out, multiplexer_2_out, or_1_out, subtractor_1_out;

  // Probe on X
  // Probe on Y
  assign and_1_out = X & Y;  // AND_Gate and_1, 32 bits wide
  assign or_1_out = X | Y;  // OR_Gate or_1, 32 bits wide
  Adder #(.width(32)) adder_1 (.a(X), .b(Y), .out(adder_1_out));  // open: cin, cout
  Subtractor #(.width(32)) subtractor_1 (.a(X), .b(Y), .out(subtractor_1_out));  // open: bin, bout
  Comparator #(.width(32)) comparator_1 (.a(X), .b(Y), .eq(Equal), .lt(comparator_1_lt));  // open: gt
  // Probe on Result
  Multiplexer #(.select(3), .width(32)) multiplexer_1 (
    .in0(and_1_out), .in1(or_1_out), .in2(adder_1_out), .in6(subtractor_1_out), .in7(multiplexer_2_out),
    .out(Result), .sel(AluOP));  // open: in3, in4, in5, en
  Multiplexer #(.width(32)) multiplexer_2 (
    .in0({32{1'b0}}), .in1(32'h1), .out(multiplexer_2_out), .sel(comparator_1_lt));  // open: en

  // Other names for the same wires on the sheet: OP[2:0] = AluOP; Result2[31:0] = Result_2

  // Notes on the sheet:
  //   不要改变此引脚区域内容，也不要改变ALU封装形式
  //   输入引脚
  //   输出引脚
endmodule

module MainControl (
  input  [5:0] in_1,
  output out_2,
  output out_3,
  output out_4,
  output out_5,
  output out_6,
  output out_7,
  output out_8,
  output [1:0] out_9,
  output PcSrc
);

  wire not_1_out, not_2_out, not_3_out, not_4_out, not_5_out, not_6_out, not_7_out, not_8_out, not_9_out,
       not_10_out, not_11_out, not_12_out, not_13_out, not_14_out, not_15_out, not_16_out, not_17_out,
       not_18_out, not_19_out, not_20_out, not_21_out;

  not not_1 (not_1_out, in_1[2]);
  not not_2 (not_2_out, in_1[0]);
  not not_3 (not_3_out, in_1[1]);
  not not_4 (not_4_out, in_1[5]);
  not not_5 (not_5_out, in_1[3]);
  not not_6 (not_6_out, in_1[4]);
  and R (out_2, not_2_out, not_3_out, not_1_out, not_5_out, not_6_out, not_4_out);
  not not_7 (not_7_out, in_1[3]);
  not not_8 (not_8_out, in_1[4]);
  not not_9 (not_9_out, in_1[2]);
  and lw (out_4, in_1[5], not_8_out, not_7_out, not_9_out, in_1[1], in_1[0]);
  not not_10 (not_10_out, in_1[4]);
  and sw (out_7, in_1[5], not_10_out, in_1[3], not_11_out, in_1[1], in_1[0]);
  not not_11 (not_11_out, in_1[2]);
  not not_12 (not_12_out, in_1[4]);
  not not_13 (not_13_out, in_1[5]);
  not not_14 (not_14_out, in_1[3]);
  and beq (out_8, not_13_out, not_12_out, not_14_out, in_1[2], not_15_out, not_17_out);
  not not_15 (not_15_out, in_1[1]);
  not not_16 (not_16_out, in_1[5]);
  not not_17 (not_17_out, in_1[0]);
  not not_18 (not_18_out, in_1[3]);
  not not_19 (not_19_out, in_1[2]);
  not not_20 (not_20_out, in_1[4]);
  and j (PcSrc, not_16_out, not_20_out, not_18_out, not_19_out, in_1[1], not_21_out);
  not not_21 (not_21_out, in_1[0]);
  or or_1 (out_3, out_4, out_7);
  or or_2 (out_5, out_2, out_4);

  assign out_6 = out_4;
  assign out_9 = {out_2, out_8};

  // Other names for the same wires on the sheet: ALUOP[1:0] = {out_2, out_8}; Branch = out_8; RegDst = out_2;
  //   ALUSrc = out_3; INS[5:0] = in_1; MemRead = out_4; MemtoReg = out_4; MemWrite = out_7; RegWrite = out_5
endmodule

module ALUcontrol (
  input  [5:0] Funct,
  input  [1:0] ALUop,
  output [2:0] ALUControl
);

  wire add_2_out, and_2_out, and_out, beq_out, not_1_out, not_2_out, not_3_out, not_4_out, not_5_out,
       not_6_out, not_7_out, not_8_out, not_9_out, not_10_out, not_11_out, not_12_out, not_13_out,
       not_14_out, not_15_out, not_16_out, not_17_out, not_18_out, or_2_out, or_4_out, or_out, r_out,
       set_on_less_than_2_out, set_on_less_than_out, sub_2_out, sub_out;

  not not_1 (not_1_out, ALUop[1]);
  not not_2 (not_2_out, ALUop[0]);
  not not_3 (not_3_out, ALUop[1]);
  and beq (beq_out, not_3_out, ALUop[0]);
  // AND_Gate lw_sw has open pins: in0=not_1_out, in1=not_2_out, out=open
  and r (r_out, ALUop[1], not_6_out);
  not not_4 (not_4_out, Funct[0]);
  not not_5 (not_5_out, Funct[1]);
  not not_6 (not_6_out, ALUop[0]);
  // AND_Gate add has open pins: in0=r_out, in1=add_2_out, out=open
  not not_7 (not_7_out, Funct[3]);
  not not_8 (not_8_out, Funct[2]);
  not not_9 (not_9_out, Funct[3]);
  and add_2 (add_2_out, not_4_out, not_5_out, not_8_out, not_9_out);
  and sub (sub_out, r_out, sub_2_out);
  not not_10 (not_10_out, Funct[2]);
  not not_11 (not_11_out, Funct[0]);
  and sub_2 (sub_2_out, not_7_out, not_10_out, Funct[1], not_11_out);
  and \and  (and_out, r_out, and_2_out);
  not not_12 (not_12_out, Funct[3]);
  not not_13 (not_13_out, Funct[1]);
  not not_14 (not_14_out, Funct[0]);
  and and_2 (and_2_out, not_12_out, Funct[2], not_13_out, not_14_out);
  and \or  (or_out, r_out, or_2_out);
  not not_15 (not_15_out, Funct[1]);
  not not_16 (not_16_out, Funct[3]);
  and or_2 (or_2_out, not_16_out, Funct[2], not_15_out, Funct[0]);
  and set_on_less_than (set_on_less_than_out, r_out, set_on_less_than_2_out);
  not not_17 (not_17_out, Funct[2]);
  not not_18 (not_18_out, Funct[0]);
  and set_on_less_than_2 (set_on_less_than_2_out, Funct[3], not_17_out, Funct[1], not_18_out);
  or or_3 (ALUControl[0], set_on_less_than_out, or_out);
  not not_19 (ALUControl[1], or_4_out);
  or or_4 (or_4_out, and_out, or_out);
  or or_5 (ALUControl[2], set_on_less_than_out, sub_out, beq_out);
endmodule
